// Logisim project LivresDesCompsants.circ as structural Verilog
module main (
);

  QuatreAUnCompresseurEW quatreauncompresseurew_1 ();  // open: OROLOGE, COMMENCER, A0, A1, A2, A3, FINI, A
  UnAQuatreDecompresseurEW unaquatredecompresseurew_1 ();  // open: OROLOGE, COMMENCER, A, A0, A1, A2, FINI, A3
  QuatreAUnCompresseurNS quatreauncompresseurns_1 ();  // open: OROLOGE, COMMENCER, A0, A1, A2, A3, FINI, A
  UnAQuatreDecompresseurNS unaquatredecompresseurns_1 ();  // open: OROLOGE, COMMENCER, A, A0, A1, A2, A3, FINI
  ZeroATroisIncremAjoutantEW zeroatroisincremajoutantew_1 ();  // open: OROLOGE, COMMENCER, FINI, S0, S1
  OneBitAjoutantEW onebitajoutantew_1 ();  // open: A, B, Cin, ACT, K, Cout
  ZeroATroisIncremAjoutantNS zeroatroisincremajoutantns_1 ();  // open: OROLOGE, COMMENCER, FINI, S0, S1
  OneBitAjoutantNS onebitajoutantns_1 ();  // open: A, B, Cin, ACT, K, Cout
  QuatreBitAjoutantEW quatrebitajoutantew_1 ();  // open: B, A, HORG, CMR, Cin, RST, FINI, K0, K1, K2, K3
endmodule

module QuatreAUnCompresseurEW (
  input  A0,
  input  A1,
  input  A2,
  input  A3,
  input  OROLOGE,
  input  COMMENCER,
  output FINI,
  output A
);

  wire [1:0] zeroatroisincremajoutantew_1_s0;

  Multiplexer #(.select(2)) multiplexer_1 (
    .in0(A0), .in1(A1), .in2(A2), .in3(A3), .out(A), .sel(zeroatroisincremajoutantew_1_s0));
  ZeroATroisIncremAjoutantEW zeroatroisincremajoutantew_1 (
    .OROLOGE(OROLOGE), .COMMENCER(COMMENCER), .FINI(FINI), .S0(zeroatroisincremajoutantew_1_s0[0]),
    .S1(zeroatroisincremajoutantew_1_s0[1]));

  // Notes on the sheet:
  //   on utilise "fini" bit avec la dernière bit pour minimaliser le delai des components sous-nivel
  //   le delai (pour ejemple un delai d'un cycle peut faire dans les components seuls qu'ont besoin de ça
endmodule

module QuatreAUnCompresseurNS (
  input  A0,
  input  A1,
  input  A2,
  input  A3,
  input  OROLOGE,
  input  COMMENCER,
  output FINI,
  output A
);

  wire [1:0] zeroatroisincremajoutantew_1_s0;

  Multiplexer #(.select(2)) multiplexer_1 (
    .in0(A0), .in1(A1), .in2(A2), .in3(A3), .out(A), .sel(zeroatroisincremajoutantew_1_s0));
  ZeroATroisIncremAjoutantEW zeroatroisincremajoutantew_1 (
    .OROLOGE(OROLOGE), .COMMENCER(COMMENCER), .FINI(FINI), .S0(zeroatroisincremajoutantew_1_s0[0]),
    .S1(zeroatroisincremajoutantew_1_s0[1]));

  // Notes on the sheet:
  //   c'est la même sauf qu'il va du nord au sud
endmodule

module UnAQuatreDecompresseurEW (
  input  OROLOGE,
  input  COMMENCER,
  input  A,
  output FINI,
  output A0,
  output A1,
  output A2,
  output A3
);

  wire [1:0] zeroatroisincremajoutantns_1_s0;

  ZeroATroisIncremAjoutantNS zeroatroisincremajoutantns_1 (
    .OROLOGE(OROLOGE), .COMMENCER(COMMENCER), .FINI(FINI), .S0(zeroatroisincremajoutantns_1_s0[0]),
    .S1(zeroatroisincremajoutantns_1_s0[1]));
  Demultiplexer #(.select(2)) demultiplexer_1 (
    .out0(A0), .out1(A1), .out2(A2), .out3(A3), .in(A), .sel(zeroatroisincremajoutantns_1_s0));
endmodule

module UnAQuatreDecompresseurNS (
  input  OROLOGE,
  input  COMMENCER,
  input  A,
  output FINI,
  output A0,
  output A1,
  output A2,
  output A3
);

  wire [1:0] zeroatroisincremajoutantns_1_s0;

  ZeroATroisIncremAjoutantNS zeroatroisincremajoutantns_1 (
    .OROLOGE(OROLOGE), .COMMENCER(COMMENCER), .FINI(FINI), .S0(zeroatroisincremajoutantns_1_s0[0]),
    .S1(zeroatroisincremajoutantns_1_s0[1]));
  Demultiplexer #(.select(2)) demultiplexer_1 (
    .out0(A0), .out1(A1), .out2(A2), .out3(A3), .in(A), .sel(zeroatroisincremajoutantns_1_s0));
endmodule

module ZeroATroisIncremAjoutantEW (
  input  OROLOGE,
  input  COMMENCER,
  output S0,
  output S1,
  output FINI
);

  wire and_2_out, d_ff_1_q, nand_1_out, or_1_out, t_ff_1_q;

  and and_1 (FINI, S1, S0);
  T_Flip_Flop t_ff_1 (.T(or_1_out), .clk(OROLOGE), .Q(t_ff_1_q));  // open: Qn, reset, preset
  or or_1 (or_1_out, FINI, COMMENCER);
  D_Flip_Flop d_ff_1 (.D(nand_1_out), .clk(and_2_out), .Q(d_ff_1_q));  // open: Qn, preset, reset
  and and_2 (and_2_out, OROLOGE, t_ff_1_q);
  J_K_Flip_Flop j_k_ff_1 (.J(d_ff_1_q), .K(d_ff_1_q), .clk(and_2_out), .Q(S0));  // open: Qn, preset, reset
  nand nand_1 (nand_1_out, S0, S1);
  J_K_Flip_Flop j_k_ff_2 (.J(S0), .K(S0), .clk(and_2_out), .Q(S1));  // open: Qn, preset, reset

  // Notes on the sheet:
  //   un formation JK simple, qui utilise un DFF pour un 1-cycle delai
  //   avec ça, il lit 00 pour un temps et n'est pas incrémenter instantement de "00" à "01"
  //   le commencer (cmr) bit peut être activé pour tout le temps petit ou grand
  //   mais, le cmr bit regarde le status pour un cycle trop long
  //   c'est NAND gate fait le 1-temps delai
endmodule

module ZeroATroisIncremAjoutantNS (
  input  OROLOGE,
  input  COMMENCER,
  output S0,
  output S1,
  output FINI
);

  wire and_2_out, d_ff_1_q, nand_1_out, or_1_out, t_ff_1_q;

  and and_1 (FINI, S1, S0);
  T_Flip_Flop t_ff_1 (.T(or_1_out), .clk(OROLOGE), .Q(t_ff_1_q));  // open: Qn, reset, preset
  or or_1 (or_1_out, FINI, COMMENCER);
  D_Flip_Flop d_ff_1 (.D(nand_1_out), .clk(and_2_out), .Q(d_ff_1_q));  // open: Qn, preset, reset
  and and_2 (and_2_out, OROLOGE, t_ff_1_q);
  J_K_Flip_Flop j_k_ff_1 (.J(d_ff_1_q), .K(d_ff_1_q), .clk(and_2_out), .Q(S0));  // open: Qn, preset, reset
  nand nand_1 (nand_1_out, S0, S1);
  J_K_Flip_Flop j_k_ff_2 (.J(S0), .K(S0), .clk(and_2_out), .Q(S1));  // open: Qn, preset, reset
endmodule

module OneBitAjoutantEW (
  input  A,
  input  B,
  input  Cin,
  input  ACT,
  output Cout,
  output K
);

  wire and_1_out, and_2_out, or_1_out, xor_1_out, xor_2_out;

  xor xor_1 (xor_1_out, A, B);
  and and_1 (and_1_out, A, B);
  and and_2 (and_2_out, xor_1_out, Cin);
  xor xor_2 (xor_2_out, xor_1_out, Cin);
  or or_1 (or_1_out, and_1_out, and_2_out);
  and and_3 (K, xor_2_out, ACT);
  and and_4 (Cout, or_1_out, ACT);

  // Notes on the sheet:
  //   1-bit tout ajoutant
  //   L'Inclusion de l'Activer est étrange mais, c'est similaire de "commencer" dans tous autres compsants
endmodule

module OneBitAjoutantNS (
  input  A,
  input  B,
  input  Cin,
  input  ACT,
  output Cout,
  output K
);

  wire and_1_out, and_2_out, or_1_out, xor_1_out, xor_2_out;

  xor xor_1 (xor_1_out, A, B);
  and and_1 (and_1_out, A, B);
  and and_2 (and_2_out, xor_1_out, Cin);
  xor xor_2 (xor_2_out, xor_1_out, Cin);
  or or_1 (or_1_out, and_1_out, and_2_out);
  and and_3 (K, xor_2_out, ACT);
  and and_4 (Cout, or_1_out, ACT);

  // Notes on the sheet:
  //   le NS du tout ajoutant
endmodule

module QuatreBitAjoutantEW (
  input  [3:0] A,
  input  HORG,
  input  CMR,
  input  [3:0] B,
  input  RST,
  input  Cin,
  output FINI,
  output K0,
  output K1,
  output K2,
  output K3
);

  wire onebitajoutantew_1_cout, onebitajoutantew_1_k, or_1_out, quatreauncompresseurew_1_a,
       quatreauncompresseurew_2_a;

  QuatreAUnCompresseurEW quatreauncompresseurew_1 (
    .OROLOGE(HORG), .COMMENCER(CMR), .A0(A[0]), .A1(A[1]), .A2(A[2]), .A3(A[3]), .FINI(FINI),
    .A(quatreauncompresseurew_1_a));
  QuatreAUnCompresseurEW quatreauncompresseurew_2 (
    .OROLOGE(HORG), .COMMENCER(CMR), .A0(B[0]), .A1(B[1]), .A2(B[2]), .A3(B[3]),
    .A(quatreauncompresseurew_2_a));  // open: FINI
  or or_1 (or_1_out, Cin, onebitajoutantew_1_cout);
  OneBitAjoutantEW onebitajoutantew_1 (
    .A(quatreauncompresseurew_1_a), .B(quatreauncompresseurew_2_a), .Cin(or_1_out), .ACT(HORG),
    .K(onebitajoutantew_1_k), .Cout(onebitajoutantew_1_cout));
  souvenir souvenir_1 (
    .OROLOGE(HORG), .COMMENCER(CMR), .Entree(onebitajoutantew_1_k), .RST(RST), .M0(K0), .M1(K1), .M2(K2),
    .M3(K3));

  // Notes on the sheet:
  //   je ne sais pas la raison que ce truc garde des values et nes autres
  //   ie A = 4, B = 8, fait 12
  //   mais M1 est 1 tous temps, et M2 changer entre 0 et 1
endmodule

module souvenir (
  input  OROLOGE,
  input  COMMENCER,
  input  Entree,
  input  RST,
  output M0,
  output M1,
  output M2,
  output M3
);

  wire d_ff_1_q, d_ff_2_q, d_ff_3_q, d_ff_4_q, demultiplexer_1_out0, demultiplexer_1_out1,
       demultiplexer_1_out2, demultiplexer_1_out3, nand_1_out, nand_2_out, nand_3_out, nand_4_out, not_1_out,
       not_2_out, zeroatroisincremajoutantns_1_fini;
  wire [1:0] zeroatroisincremajoutantns_1_s0;

  not not_1 (not_1_out, zeroatroisincremajoutantns_1_s0[0]);
  not not_2 (not_2_out, zeroatroisincremajoutantns_1_s0[1]);
  Demultiplexer #(.select(2)) demultiplexer_1 (
    .out0(demultiplexer_1_out0), .out1(demultiplexer_1_out1), .out2(demultiplexer_1_out2),
    .out3(demultiplexer_1_out3), .in(Entree), .sel(zeroatroisincremajoutantns_1_s0));
  ZeroATroisIncremAjoutantNS zeroatroisincremajoutantns_1 (
    .OROLOGE(OROLOGE), .COMMENCER(COMMENCER), .FINI(zeroatroisincremajoutantns_1_fini),
    .S0(zeroatroisincremajoutantns_1_s0[0]), .S1(zeroatroisincremajoutantns_1_s0[1]));
  D_Flip_Flop #(.trigger("low")) d_ff_1 (
    .D(demultiplexer_1_out0), .clk(nand_1_out), .Q(d_ff_1_q), .reset(RST));  // open: Qn, preset
  nand nand_1 (nand_1_out, not_1_out, not_2_out);
  D_Flip_Flop #(.trigger("low")) d_ff_2 (
    .D(demultiplexer_1_out1), .clk(nand_2_out), .Q(d_ff_2_q), .reset(RST));  // open: Qn, preset
  nand nand_2 (nand_2_out, not_2_out, zeroatroisincremajoutantns_1_s0[0]);
  D_Flip_Flop #(.trigger("low")) d_ff_3 (
    .D(demultiplexer_1_out2), .clk(nand_3_out), .Q(d_ff_3_q), .reset(RST));  // open: Qn, preset
  nand nand_3 (nand_3_out, zeroatroisincremajoutantns_1_s0[1], not_1_out);
  D_Flip_Flop #(.trigger("low")) d_ff_4 (
    .D(demultiplexer_1_out3), .clk(nand_4_out), .Q(d_ff_4_q), .reset(RST));  // open: Qn, preset
  nand nand_4 (nand_4_out, zeroatroisincremajoutantns_1_s0[0], zeroatroisincremajoutantns_1_s0[1]);
  D_Flip_Flop d_ff_5 (.D(d_ff_1_q), .clk(zeroatroisincremajoutantns_1_fini), .Q(M0), .reset(RST));  // open: Qn, preset
  D_Flip_Flop d_ff_6 (.D(d_ff_2_q), .clk(zeroatroisincremajoutantns_1_fini), .Q(M1), .reset(RST));  // open: Qn, preset
  D_Flip_Flop d_ff_7 (.D(d_ff_3_q), .clk(zeroatroisincremajoutantns_1_fini), .Q(M2), .reset(RST));  // open: Qn, preset
  D_Flip_Flop d_ff_8 (.D(d_ff_4_q), .clk(zeroatroisincremajoutantns_1_fini), .Q(M3), .reset(RST));  // open: Qn, preset

  // Notes on the sheet:
  //   les choses ci-dessus sont essentiellement un Demux lol 
  //   je les corrigerai plus tard
  //   M0
  //   M1
  //   M2
  //   M3
endmodule

module souvenir2 (
  input  ENTREE,
  input  OROLOGE,
  input  COMMENCER,
  input  in_4,
  output FINI
);

  wire demultiplexer_1_out0, demultiplexer_1_out1, demultiplexer_1_out2, demultiplexer_1_out3,
       demultiplexer_2_out0, demultiplexer_2_out1, demultiplexer_2_out2, demultiplexer_2_out3;
  wire [1:0] zeroatroisincremajoutantew_1_s0;

  Demultiplexer #(.select(2)) demultiplexer_1 (
    .out0(demultiplexer_1_out0), .out1(demultiplexer_1_out1), .out2(demultiplexer_1_out2),
    .out3(demultiplexer_1_out3), .in(ENTREE), .sel(zeroatroisincremajoutantew_1_s0));
  Demultiplexer #(.select(2)) demultiplexer_2 (
    .out0(demultiplexer_2_out0), .out1(demultiplexer_2_out1), .out2(demultiplexer_2_out2),
    .out3(demultiplexer_2_out3), .in(1'b1), .sel(zeroatroisincremajoutantew_1_s0));
  ZeroATroisIncremAjoutantEW zeroatroisincremajoutantew_1 (
    .OROLOGE(OROLOGE), .COMMENCER(COMMENCER), .FINI(FINI), .S0(zeroatroisincremajoutantew_1_s0[0]),
    .S1(zeroatroisincremajoutantew_1_s0[1]));
  D_Flip_Flop #(.trigger("high")) d_ff_1 (
    .D(demultiplexer_1_out0), .clk(demultiplexer_2_out0), .reset(in_4));  // open: Q, Qn, preset
  D_Flip_Flop d_ff_2 (.D(demultiplexer_1_out1), .clk(demultiplexer_2_out1), .reset(in_4));  // open: Q, Qn, preset
  D_Flip_Flop d_ff_3 (.D(demultiplexer_1_out2), .clk(demultiplexer_2_out2), .reset(in_4));  // open: Q, Qn, preset
  D_Flip_Flop d_ff_4 (.D(demultiplexer_1_out3), .clk(demultiplexer_2_out3), .reset(in_4));  // open: Q, Qn, preset
endmodule

module test (
  input  [3:0] A,
  input  HORG,
  input  CMR,
  input  [3:0] B,
  input  RST,
  input  Cin,
  output FINI,
  output K0,
  output K1,
  output K2,
  output K3
);

  wire onebitajoutantew_1_cout, onebitajoutantew_1_k, or_1_out, quatreauncompresseurew_1_a,
       quatreauncompresseurew_2_a;

  QuatreAUnCompresseurEW quatreauncompresseurew_1 (
    .OROLOGE(HORG), .COMMENCER(CMR), .A0(A[0]), .A1(A[1]), .A2(A[2]), .A3(A[3]), .FINI(FINI),
    .A(quatreauncompresseurew_1_a));
  QuatreAUnCompresseurEW quatreauncompresseurew_2 (
    .OROLOGE(HORG), .COMMENCER(CMR), .A0(B[0]), .A1(B[1]), .A2(B[2]), .A3(B[3]),
    .A(quatreauncompresseurew_2_a));  // open: FINI
  or or_1 (or_1_out, Cin, onebitajoutantew_1_cout);
  OneBitAjoutantEW onebitajoutantew_1 (
    .A(quatreauncompresseurew_1_a), .B(quatreauncompresseurew_2_a), .Cin(or_1_out), .ACT(HORG),
    .K(onebitajoutantew_1_k), .Cout(onebitajoutantew_1_cout));
endmodule

module ALU (
  input  [3:0] A,
  input  [2:0] OP_CODE,
  input  [3:0] B
);

  wire [3:0] demultiplexer_1_out0, demultiplexer_2_out0;

  Demultiplexer #(.select(3), .width(4)) demultiplexer_1 (
    .out0(demultiplexer_1_out0), .in(A), .sel(OP_CODE));  // open: out1, out2, out3, out4, out5, out6, out7
  Demultiplexer #(.select(3), .width(4)) demultiplexer_2 (
    .out0(demultiplexer_2_out0), .in(B), .sel(OP_CODE));  // open: out1, out2, out3, out4, out5, out6, out7
  QuatreBitAjoutantEW quatrebitajoutantew_1 (
    .B(demultiplexer_2_out0), .A(demultiplexer_1_out0));  // open: HORG, CMR, Cin, RST, FINI, K0, K1, K2, K3

  // Notes on the sheet:
  //   Ajoutant - 00
  //   Subtracteur - 01
  //   OR Logique - 02
  //   Ajoutant, Subtracteur, OR Logique, AND Logique, SRL, SLL, 2s Comp, 1s Comp
endmodule

module DeuxCompEW (
  input  [3:0] A,
  input  in_2,
  input  OROLOGE,
  input  COMMENCER,
  output out_5
);

  QuatreBitAjoutantEW quatrebitajoutantew_1 (
    .B(A), .A(4'b0001), .HORG(OROLOGE), .CMR(COMMENCER), .Cin(in_2), .RST(out_5));  // open: FINI, K0, K1, K2, K3
endmodule

module PC (
  input  INCREM,
  input  FINI,
  input  COMMENCER
);

  wire d_ff_1_q, j_k_ff_1_q, j_k_ff_2_q, j_k_ff_3_q, j_k_ff_4_q, undriven;

  D_Flip_Flop d_ff_1 (.D(undriven), .Q(d_ff_1_q));  // open: clk, Qn, preset, reset
  J_K_Flip_Flop j_k_ff_1 (.J(1'b1), .K(d_ff_1_q), .clk(INCREM), .Q(j_k_ff_1_q));  // open: Qn, preset, reset
  T_Flip_Flop t_ff_1 ();  // open: T, clk, Q, Qn, reset, preset
  // OR_Gate or_1 has open pins: in0=FINI, in1=COMMENCER, out=open
  J_K_Flip_Flop j_k_ff_2 (.J(1'b1), .K(1'b1), .clk(j_k_ff_1_q), .Q(j_k_ff_2_q));  // open: Qn, preset, reset
  J_K_Flip_Flop j_k_ff_3 (.J(1'b1), .K(1'b1), .clk(j_k_ff_2_q), .Q(j_k_ff_3_q));  // open: Qn, preset, reset
  J_K_Flip_Flop j_k_ff_4 (.J(1'b1), .K(1'b1), .clk(j_k_ff_3_q), .Q(j_k_ff_4_q));  // open: Qn, preset, reset
endmodule
