// Logisim project ChesapeakeArchitectureBlocks.circ as structural Verilog
module main (
  input  clk,
  input  [31:0] in_2
);

  wire controller_sitter_1_ir_write;
  wire [1:0] controller_sitter_1_alu_src_a, controller_sitter_1_alu_src_b, controller_sitter_1_ir_source;
  wire [31:0] ir_reg_q, multiplexer_1_out, multiplexer_2_out, multiplexer_3_out, reg_a_q, reg_b_q;

  Multiplexer #(.select(2), .width(32)) multiplexer_1 (
    .out(multiplexer_1_out), .sel(controller_sitter_1_ir_source));  // open: in0, in1, in2, in3
  Register #(.width(32)) ir_reg (
    .D(multiplexer_1_out), .en(controller_sitter_1_ir_write), .clk(clk), .Q(ir_reg_q));  // open: clr
  controller_sitter controller_sitter_1 (
    .ir_31_0(ir_reg_q), .alu_src_a(controller_sitter_1_alu_src_a), .alu_src_b(controller_sitter_1_alu_src_b),
    .ir_write(controller_sitter_1_ir_write), .ir_source(controller_sitter_1_ir_source));  // open: in_2, in_3, in_4, in_5
  Multiplexer #(.select(2), .width(32)) multiplexer_2 (
    .out(multiplexer_2_out), .sel(controller_sitter_1_alu_src_a));  // open: in0, in1, in2, in3
  Multiplexer #(.select(2), .width(32)) multiplexer_3 (
    .out(multiplexer_3_out), .sel(controller_sitter_1_alu_src_b));  // open: in0, in1, in2, in3
  Register #(.width(32)) reg_a (.D(multiplexer_2_out), .Q(reg_a_q));  // open: en, clk, clr
  Register #(.width(32)) reg_b (.D(multiplexer_3_out), .Q(reg_b_q));  // open: en, clk, clr
endmodule

module controller_sitter (
  input  [31:0] ir_31_0,
  input  [1:0] in_2,
  input  [1:0] in_3,
  input  in_4,
  input  [1:0] in_5,
  output [1:0] alu_src_a,
  output [1:0] alu_src_b,
  output ir_write,
  output [1:0] ir_source
);


  assign alu_src_a = in_2;
  assign alu_src_b = in_3;
  assign ir_source = in_5;
  assign ir_write = in_4;
endmodule
